// Logisim project IT012_Lab01_24520935.circ as structural Verilog
module TN1 (
  input  A,
  input  B,
  input  C,
  output A_prime,
  output AND,
  output OR,
  output NAND,
  output NOR,
  output XOR,
  output XNOR,
  output XOR3,
  output NAND3,
  output CHAIN
);

  wire nand_3_out;

  not not_1 (A_prime, A);
  and and_1 (AND, A, B);
  or or_1 (OR, A, B);
  nand nand_1 (NAND, A, B);
  nor nor_1 (NOR, A, B);
  xor xor_1 (XOR, A, B);
  xnor xnor_1 (XNOR, A, B);
  ExactlyOne xor_2 (.out(XOR3), .in0(A), .in1(C), .in2(B));
  nand nand_2 (NAND3, A, C, B);
  nand nand_3 (nand_3_out, A, B);
  nand nand_4 (CHAIN, nand_3_out, C);
endmodule

module TN2 (
  input  x,
  input  y,
  input  z,
  output EQ1,
  output EQ2,
  output EQ3,
  output EQ4,
  output EQ5
);

  wire and_1_out, and_2_out, and_3_out, and_4_out, and_5_out, and_6_out, not_1_out, not_2_out, not_3_out,
       not_4_out, or_1_out, or_2_out, or_3_out, or_4_out;

  not not_1 (not_1_out, x);
  not not_2 (not_2_out, y);
  or or_1 (or_1_out, x, y);
  and and_1 (and_1_out, not_1_out, not_2_out);
  and and_2 (and_2_out, x, y);
  and and_3 (and_3_out, not_1_out, not_2_out);
  and and_4 (and_4_out, y, z);
  or or_2 (or_2_out, x, z);
  and and_5 (and_5_out, not_1_out, y);
  not not_3 (not_3_out, or_1_out);
  not not_4 (not_4_out, and_2_out);
  or or_3 (or_3_out, and_4_out, x);
  and and_6 (and_6_out, or_2_out, or_1_out);
  or or_4 (or_4_out, and_5_out, x);
  xnor xnor_1 (EQ1, not_3_out, and_1_out);
  xnor xnor_2 (EQ2, not_4_out, and_3_out);
  xnor xnor_3 (EQ3, or_3_out, and_6_out);
  xnor xnor_4 (EQ4, or_4_out, x);
  xnor xnor_5 (EQ5, or_4_out, or_1_out);
endmodule

module Warmup (
  input  B,
  input  A,
  output F
);

  wire not_1_out;

  not not_1 (not_1_out, B);
  and and_1 (F, not_1_out, A);
endmodule

module TN3 (
  input  A,
  input  B,
  input  C,
  input  D,
  output A_prime,
  output B_prime,
  output C_prime,
  output D_prime,
  output F
);

  wire and_1_out, and_2_out, and_3_out, and_4_out, and_5_out, and_6_out;

  not not_1 (A_prime, A);
  not not_2 (B_prime, B);
  not not_3 (C_prime, C);
  not not_4 (D_prime, D);
  and and_1 (and_1_out, A_prime, B_prime, C, D_prime);
  and and_2 (and_2_out, A_prime, B_prime, C, D);
  and and_3 (and_3_out, A_prime, B, C_prime, D);
  and and_4 (and_4_out, A_prime, B, C, D);
  and and_5 (and_5_out, A, B_prime, C, D);
  and and_6 (and_6_out, A, B, C_prime, D);
  or or_1 (F, and_1_out, and_2_out, and_3_out, and_4_out, and_5_out, and_6_out);
endmodule

module TN4 (
  input  A,
  input  B,
  input  C,
  input  D,
  output A_prime,
  output B_prime,
  output C_prime,
  output D_prime,
  output F_can,
  output F_sop,
  output F_pos
);

  wire and_1_out, and_2_out, and_3_out, and_4_out, and_5_out, and_6_out, and_7_out, and_8_out, and_9_out,
       and_10_out, or_1_out, or_2_out, or_3_out, or_4_out;

  not not_1 (A_prime, A);
  not not_2 (B_prime, B);
  not not_3 (C_prime, C);
  not not_4 (D_prime, D);
  and and_1 (and_1_out, A_prime, B_prime, C, D_prime);
  and and_2 (and_2_out, A_prime, B_prime, C, D);
  and and_3 (and_3_out, A_prime, B, C_prime, D);
  and and_4 (and_4_out, A_prime, B, C, D);
  and and_5 (and_5_out, A, B_prime, C, D);
  and and_6 (and_6_out, A, B, C_prime, D);
  and and_7 (and_7_out, A_prime, B_prime, C);
  and and_8 (and_8_out, B_prime, C, D);
  and and_9 (and_9_out, B, C_prime, D);
  and and_10 (and_10_out, A_prime, C, D);
  or or_1 (or_1_out, B, C);
  or or_2 (or_2_out, A_prime, D);
  or or_3 (or_3_out, B_prime, D);
  or or_4 (or_4_out, A_prime, B_prime, C_prime);
  or or_5 (F_can, and_1_out, and_2_out, and_3_out, and_4_out, and_5_out, and_6_out);
  or or_6 (F_sop, and_7_out, and_8_out, and_9_out, and_10_out);
  and and_11 (F_pos, or_1_out, or_2_out, or_3_out, or_4_out);
endmodule

module TN5 (
  input  A,
  input  B,
  input  C,
  output F
);

  wire xor_1_out;

  xor xor_1 (xor_1_out, A, B);
  xor xor_2 (F, xor_1_out, C);
endmodule
